# Fritzing sketch dio_brick (saved by Fritzing 0.8.7b)
circuit board: 2.7533cm x 4.42831cm
perfboards: 1

parts:
  R1 = Resistor [tolerance=±5% resistance=47k package=THT]
  IC1 = IC, DIP package, 20 pins [chip_label=G2553]
  PWR = female pin header, 2 pins [form="♀ (female)"]
  I2C = female pin header, 3 pins [form="♀ (female)"]
  R2 = Resistor [tolerance=±5% resistance=220 package=THT]
  LED1 = LED - 3mm [color="Red (633nm)" package="3 mm [THT]"]
  R3 = Resistor [tolerance=±5% resistance=220 package=THT]
  LED2 = LED - 3mm [color="Red (633nm)" package="3 mm [THT]"]
  PROG = female pin header, 5 pins [form="♀ (female)"]
  DO1 = female pin header, 2 pins [form="♀ (female)"]
  DO2 = female pin header, 2 pins [form="♀ (female)"]
  DO3 = female pin header, 2 pins [form="♀ (female)"]
  DO4 = female pin header, 2 pins [form="♀ (female)"]
  DI1 = female pin header, 2 pins [form="♀ (female)"]
  DI2 = female pin header, 2 pins [form="♀ (female)"]
  DI3 = female pin header, 2 pins [form="♀ (female)"]
  DI4 = female pin header, 2 pins [form="♀ (female)"]

nets:
  3.3V/VCC: R1.Pin_0, IC1.pin1, PWR.pin1
  RST: R1.Pin_1, IC1.pin16, PROG.pin1
  DO1: IC1.pin2, DO1.pin1
  RX: IC1.pin3, PROG.pin3
  TX: IC1.pin4, PROG.pin4
  DO2: IC1.pin5, DO2.pin1
  DO3: IC1.pin6, DO3.pin1
  DO4: IC1.pin7, DO4.pin1
  DI1: IC1.pin8, DI1.pin1
  DI2: IC1.pin9, DI2.pin1
  DI3: IC1.pin10, DI3.pin1
  DI4: IC1.pin11, DI4.pin1
  LED2: IC1.pin12, R3.Pin_1
  LED1: IC1.pin13, R2.Pin_1
  SDL: IC1.pin14, I2C.pin1
  SDA: IC1.pin15, I2C.pin2
  TST: IC1.pin17, PROG.pin2
  GND: IC1.pin20, PWR.pin2, I2C.pin3, LED1.cathode, LED2.cathode, PROG.pin5, DO1.pin2, DO2.pin2, DO3.pin2, DO4.pin2, DI1.pin2, DI2.pin2, DI3.pin2, DI4.pin2
  N1: R2.Pin_0, LED1.anode
  N2: R3.Pin_0, LED2.anode

notes:
  gpio.kaltpost.de
  Bric(k)-o-lage
